# Fritzing sketch RailBoxCompact-5770-1007.03 (saved by Fritzing 0.9.3b)
circuit board: 7.88cm x 6.5cm
breadboards: 1

parts:
  J5 = molex pin header, 10 pins [form=molex]
  J6 = male pin header, 3 pins [form="♂ (male)"]
  J7 = RJ11 Jack [package=rj11-6]
  R1 = Resistor [tolerance=±5% resistance=220k package=THT]
  R2 = Resistor [tolerance=±5% resistance=1M package=THT]
  S1 = Pushbutton [package="[THT]"]
  R3 = Resistor [tolerance=±5% resistance=10k package=THT]
  J9 = male pin header, 10 pins [form="♂ (male)"]
  ESP8266_HUZZAH = Adafruit Feather HUZZAH ESP8266 [part_number="Adafruit #2821"]
  J10 = male pin header, 3 pins [form="♂ (male)"]
  J11 = Screw terminal - 2 pins [package=THT]

nets:
  N1: J5.pin1, J6.pin2, J9.pin1, ESP8266_HUZZAH.VBUS, J11.pin2
  N2: J5.pin2, J5.pin5, J5.pin8, J7.5, R3.Pin_0, J9.pin2, J9.pin5, J9.pin8, ESP8266_HUZZAH.3.3V, J10.pin3
  N3: J5.pin3, J5.pin6, J5.pin9, J6.pin3, J7.4, R1.Pin_0, S1.Pin_1, S1.Pin_2, J9.pin3, J9.pin6, J9.pin9, ESP8266_HUZZAH.GND, J10.pin1, J11.pin1
  N4: J5.pin4, J5.pin7, J5.pin10, J7.3, J9.pin4, J9.pin7, J9.pin10, ESP8266_HUZZAH.GPIO14/SCK, J10.pin2
  N5: J6.pin1, R2.Pin_1
  N6: R1.Pin_1, R2.Pin_0, ESP8266_HUZZAH.ADC
  N7: S1.Pin_3, S1.Pin_4, R3.Pin_1, ESP8266_HUZZAH.GPIO15

notes:
  PID: 5770-xx - Rev: 1.0
  IoThingsWare
  PID: 5770-1007-03
  5v
  3.3v
  GND

custom parts:
  Adafruit Feather HUZZAH ESP8266: his is the Adafruit Feather HUZZAH ESP8266 - our take on an 'all-in-one' ESP8266 WiFi development board with built in USB and battery charging. Its an ESP8266 WiFi module with all the extras you need, ready to rock! We have other boards in the Feather family, check'em out here. At the Feather HUZZAH's heart is an ESP8266 WiFi microcontroller clocked at 80 MHz and at 3.3V logic. This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
